# Fritzing sketch Cowlib-prototype_oled (saved by Fritzing 0.9.6b)
breadboards: 1

parts:
  Composant1 = Adafruit HUZZAH32 ESP32 Feather [part_number="Adafruit #3405"]
  LED1 = RGB LED (com. cathode, rgb) [package="5 mm [THT]"]
  Composant3 = RFID-RC522-v2
  R1 = Resistor [tolerance=±5% power=0.25 resistance=220 package=THT]
  R2 = Resistor [tolerance=±5% power=0.25 resistance=220 package=THT]
  R3 = Resistor [tolerance=±5% power=0.25 resistance=220 package=THT]
  OLED2 = SSD1306 0.96in 128x64 I2C Monochrome OLED Display

nets:
  N1: Composant1.MISO, Composant3.MISO
  N2: Composant1.MOSI, Composant3.MOSI
  N3: Composant1.SCK, Composant3.SCK
  GND: Composant1.GND, Composant3.GND, OLED2.GND
  3.3V: Composant1.3.3V, LED1.common_cathode, Composant3.3.3V, OLED2.VCC
  N4: Composant1.IO13_A12, Composant3.RST
  N5: Composant1.IO12_A11, Composant3.SDA
  N6: Composant1.IO15_A8, R3.Pin_1
  N7: Composant1.IO32_A7, R2.Pin_1
  N8: Composant1.IO14_A6, R1.Pin_1
  N9: Composant1.SCL, OLED2.SCL
  N10: Composant1.SDA, OLED2.SDA
  N11: LED1.red_anode, R1.Pin_0
  N12: LED1.green_anode, R2.Pin_0
  N13: LED1.blue_anode, R3.Pin_0

notes:
  3.3V
  SDA - SCK - MOSI - MISO - (IRQ) - GND - RST - 3.3V
  GND - 3.3V - SCL - SDA

custom parts:
  RFID-RC522-v2: A simple China made RFID-RC522 Reader; do check the pin labels, as this is a MFRC522 based clone.
